# Fritzing sketch schematic (saved by Fritzing 0.9.3b)
breadboards: 2

parts:
  Part1 = Arduino Uno (Rev3) - ICSP
  R1 = Temperature Sensor (Thermistor) [thermistor_type=NTC package=THT]
  R2 = Resistor [tolerance=±5% resistance=10k package="2010 [SMD]"]
  U1 = LCD-16X2 [package=lcd-16x2_noholes]
  R3 = Resistor [tolerance=±5% resistance=2.2k package="2010 [SMD]"]
  R4 = Resistor [tolerance=±5% resistance=220 package="2010 [SMD]"]
  RGB-LED1 = RGB LED (com. cathode, rgb) [package="5 mm [THT]"]
  J1 = Piezo Speaker
  IC1 = IC, DIP package, 8 pins [chip_label=IC]  # not connected

nets:
  N1: Part1.A0, R1.pin_0, R2.Pin_1
  N2: Part1.D8, RGB-LED1.red_anode
  N3: Part1.D9_PWM, RGB-LED1.green_anode
  N4: Part1.D10_PWM/SS, RGB-LED1.blue_anode
  N5: Part1.D11_PWM/MOSI, U1.E
  N6: Part1.D12/MISO, U1.RS
  GND: Part1.GND, R2.Pin_0, U1.VSS, U1.R_W, U1.K, R3.Pin_0, RGB-LED1.common_cathode, J1.pin2
  N7: Part1.D2, U1.DB7
  N8: Part1.D3_PWM, U1.DB6
  N9: Part1.D4, U1.DB5
  N10: Part1.D5_PWM, U1.DB4
  N11: Part1.D7, J1.pin1
  5V: Part1.5V, R1.pin_1, U1.VDD, R4.Pin_0
  N12: U1.VO, R3.Pin_1
  N13: U1.A, R4.Pin_1
